// Logisim project project.circ as structural Verilog
module PC (
  input  [31:0] imm_b,
  input  [31:0] imm_j,
  input  [31:0] rs1_val,
  input  clk,
  input  [31:0] imm_i,
  input  reset,
  input  branch_taken,
  input  jump,
  input  jalr,
  output [31:0] pc_out,
  output [31:0] pc_plus_4,
  output [31:0] pc_next
);

  wire [31:0] adder_1_out, adder_3_out, adder_4_out, and_1_out, multiplexer_1_out, multiplexer_2_out;

  Register #(.width(32)) pc_reg (.D(pc_next), .en(1'b1), .clk(clk), .Q(pc_out), .clr(reset));
  Adder #(.width(32)) adder_1 (.a(rs1_val), .b(imm_i), .out(adder_1_out));  // open: cin, cout
  Adder #(.width(32)) adder_2 (.a(pc_out), .b(32'h4), .out(pc_plus_4));  // open: cin, cout
  Adder #(.width(32)) adder_3 (.a(pc_out), .b(imm_b), .out(adder_3_out));  // open: cin, cout
  Adder #(.width(32)) adder_4 (.a(pc_out), .b(imm_j), .out(adder_4_out));  // open: cin, cout
  assign and_1_out = adder_1_out & 32'hfffffffe;  // AND_Gate and_1, 32 bits wide
  Multiplexer #(.width(32)) multiplexer_1 (
    .in0(pc_plus_4), .in1(adder_3_out), .out(multiplexer_1_out), .sel(branch_taken));
  Multiplexer #(.width(32)) multiplexer_2 (
    .in0(multiplexer_1_out), .in1(adder_4_out), .out(multiplexer_2_out), .sel(jump));
  Multiplexer #(.width(32)) multiplexer_3 (.in0(multiplexer_2_out), .in1(and_1_out), .out(pc_next), .sel(jalr));
endmodule

module imem (
);

  ROM rom_1 ();  // open: addr, data
endmodule

module immgen (
  input  [31:0] instr,
  input  [2:0] imm_sel,
  output [31:0] imm_out
);

  wire [31:0] bit_extender_1_out;

  assign bit_extender_1_out = {{20{instr[31]}}, instr[31:20]};  // Bit_Extender bit_extender_1
  Bit_Extender #(.in_width(13), .out_width(32)) bit_extender_2 (.in({instr[31], instr[7], instr[30:25], instr[11:8], 1'b0}));  // open: out
  Bit_Extender #(.in_width(21), .out_width(32)) bit_extender_3 (.in({instr[31], instr[19:12], instr[20], instr[30:21], 1'b0}));  // open: out
  Bit_Extender #(.in_width(12), .out_width(32)) bit_extender_4 (.in({instr[7], instr[11:8], instr[31:25]}));  // open: out

  // Other names for the same wires on the sheet: p11_8[3:0] = instr[11:8]; p7 = instr[7]; p30_21[9:0] = instr[30:21];
  //   p31_12[19:0] = instr[31:12]; p30_25[5:0] = instr[30:25]; p20 = instr[20]; p19_12[7:0] = instr[19:12];
  //   p31 = instr[31]; p0 = instr[0]

  // Notes on the sheet:
  //   type-i
  //   type-B
  //   type-j
  //   type-s
  //   type-u
endmodule
